# Fritzing sketch babyduino_no_clock (saved by Fritzing 0.7.11b)
breadboards: 1

parts:
  IC1 = ATMega8 [package=DIL]
  IC2 = FTDI [package=SIL]
  D1 = Rectifier Diode [part_number=1N4001 package="300 mil [THT]"]
  J1 = male pin header, 2 pins [form="♂ (male)"]
  R1 = Resistor [tolerance=±5% resistance=10k package=THT]
  C1 = Ceramic Capacitor [capacitance=100nF package="100 mil [THT, multilayer]"]
  R2 = Resistor [tolerance=±5% resistance=220 package=THT]
  LED1 = LED - 5mm [color="Red (633nm)" package="5 mm [THT]"]
  D2 = Rectifier Diode [part_number=1N4001 package="300 mil [THT]"]

nets:
  N1: IC1.RESET/PC6, R1.Pin_1
  N2: IC1.Rx/PD0, IC2.RX
  N3: IC1.Tx/PD1, IC2.TX
  VCC: IC1.VCC, IC1.AVCC, D1.cathode, R1.Pin_0, C1.1, D2.cathode
  GND: IC1.GND, IC2.GND/Black, J1.pin1, C1.0, LED1.cathode
  N4: IC1.SCK/PB5, R2.Pin_0
  N5: IC2.VCC, D1.anode
  N6: J1.pin2, D2.anode
  N7: R2.Pin_1, LED1.anode

notes:
  Babyduino, Babyduino (Internal Clock), 1A
