# Fritzing sketch prog_adaptor (saved by Fritzing 0.7.11b)
breadboards: 1

parts:
  IC1 = ATMega8 [package=DIL]
  XTAL1 = Crystal [frequency="16 Mhz" package=THT]
  C1 = Ceramic Capacitor [capacitance=22pF package="100 mil [THT, multilayer]"]
  C2 = Ceramic Capacitor [capacitance=22pF package="100 mil [THT, multilayer]"]
  IC2 = AVRISP [package=SIL]

nets:
  N1: IC1.RESET/PC6, IC2.RST
  VCC: IC1.VCC, IC1.AVCC, IC2.VCC
  GND: IC1.GND, C1.0, C2.0, IC2.GND
  N2: IC1.XTAL1/TOSC1/PB6, XTAL1.pin_0, C1.1
  N3: IC1.XTAL2/TOSC2/PB7, XTAL1.pin_1, C2.1
  N4: IC1.MOSI/OC2/PB3, IC2.MOSI
  N5: IC1.MISO/PB4, IC2.MISO
  N6: IC1.SCK/PB5, IC2.SCK

notes:
  AVR Programming Adaptor, Programming Adaptor for AVR/ATMega Chips, 1B
